# Fritzing sketch Magnet (saved by Fritzing 0.9.3b)
breadboards: 1

parts:
  R2 = Resistor [tolerance=±5% resistance=10k package=THT]
  T1 = LM35 Temperature Sensor [package="TO92 [THT]"]
  Part1 = Arduino Uno (Rev3)

nets:
  N1: R2.Pin_0, T1.+Vs, Part1.5V
  N2: R2.Pin_1, T1.GND, Part1.D3_PWM
  N3: T1.Vout, Part1.GND

notes:
  NOTE: The icon for the sensor is a temperature sensor, not a Hall Effect magnetic sensor. I couldn't find one in the Fritzing libraries for the Hall Effect, so just used this for the schematic since it has 3 pins and looks similar. Don't rely on the specs for this part!
