# Fritzing sketch Temperature (saved by Fritzing 0.9.3b)
breadboards: 1

parts:
  T1 = LM35 Temperature Sensor [package="TO92 [THT]"]
  Part1 = Arduino Uno (Rev3)

nets:
  N1: T1.+Vs, Part1.5V
  N2: T1.Vout, Part1.A1
  GND: T1.GND, Part1.GND

notes:
  Be CAREFUL !
  You must get the 5V and GND pins oriented correctly !!!
  If you reverse them, you can a) burn your finger if you touch it, and b) fry the sensor.
  Note the orientation of the sensor -- with the flat side (the side with the silk-screened labels) facing you, 5V is on the left and GND is on the right.
  Note !
  The temperature sensor is an ANALOG sensor, not digital like the magnet or button inputs.
  It must get connected to an ANALOG pin on the Arduino -- they are laberled A0 - A5.
