# Fritzing sketch Button3 (saved by Fritzing 0.9.3b)
breadboards: 1

parts:
  S1 = Pushbutton [package="[THT]"]
  Part1 = Arduino Uno (Rev3)
  S2 = Pushbutton [package="[THT]"]
  S3 = Pushbutton [package="[THT]"]
  R2 = Resistor [tolerance=±5% resistance=220 package=THT]
  R3 = Resistor [tolerance=±5% resistance=220 package=THT]
  R4 = Resistor [tolerance=±5% resistance=220 package=THT]
  LED2 = LED - 3mm [color="Red (633nm)" package="3 mm [THT]"]
  LED3 = LED - 3mm [color="Red (633nm)" package="3 mm [THT]"]
  LED1 = LED - 3mm [color="Red (633nm)" package="3 mm [THT]"]
  R1 = Resistor [tolerance=±5% resistance=10k package=THT]

nets:
  N1: S1.Pin_1, S1.Pin_2, Part1.5V
  N2: S1.Pin_3, S1.Pin_4, Part1.D2, R1.Pin_0
  N3: Part1.D11_PWM/MOSI, R4.Pin_0
  N4: Part1.D12/MISO, R3.Pin_0
  N5: Part1.D13/SCK, R2.Pin_0
  N6: Part1.GND, S2.Pin_3, S2.Pin_4, S3.Pin_3, S3.Pin_4, LED2.cathode, LED3.cathode, LED1.cathode, R1.Pin_1
  N7: Part1.D3_PWM, S2.Pin_1, S2.Pin_2
  N8: Part1.D4, S3.Pin_1, S3.Pin_2
  N9: R2.Pin_1, LED1.anode
  N10: R3.Pin_1, LED2.anode
  N11: R4.Pin_1, LED3.anode
