# Fritzing sketch WildCardPOT (saved by Fritzing 0.9.3b)
breadboards: 1

parts:
  Part1 = Arduino Uno (Rev3)
  R3 = TRIMPOT [package=3386u]

nets:
  N1: Part1.A4/SDA, R3.WIPER
  N2: Part1.5V, R3.CW
  N3: Part1.GND, R3.CCW
